// Logisim project Full_Adder.circ as structural Verilog: 2 circuits, main circuit main
module main (
  input  [3:0] A,
  input  [3:0] B,
  output [3:0] Result,
  output out_4
);

  wire full_adder_1_cout, full_adder_2_cout, full_adder_3_cout, full_adder_4_cout;

  Full_Adder full_adder_1 (.A(A[0]), .B(B[0]), .Result(Result[0]), .Cout(full_adder_1_cout));  // open: Cin
  Full_Adder full_adder_2 (.Cin(full_adder_1_cout), .A(A[1]), .B(B[1]), .Result(Result[1]), .Cout(full_adder_2_cout));
  Full_Adder full_adder_3 (.Cin(full_adder_2_cout), .A(A[2]), .B(B[2]), .Result(Result[2]), .Cout(full_adder_3_cout));
  Full_Adder full_adder_4 (.Cin(full_adder_3_cout), .A(A[3]), .B(B[3]), .Result(Result[3]), .Cout(full_adder_4_cout));
  xor xor_1 (out_4, full_adder_3_cout, full_adder_4_cout);

  // Notes on the sheet:
  //   Overflow?
endmodule

module Full_Adder (
  input  Cin,
  input  A,
  input  B,
  output Result,
  output Cout
);

  wire and_1_out, and_2_out, xor_1_out;

  xor xor_1 (xor_1_out, A, B);
  xor xor_2 (Result, xor_1_out, Cin);
  and and_1 (and_1_out, Cin, xor_1_out);
  and and_2 (and_2_out, B, A);
  or or_1 (Cout, and_1_out, and_2_out);
endmodule
